// Logisim project FULL SUB.circ as structural Verilog: 1 circuit, main circuit main
module main (
  input  A,
  input  B,
  input  C,
  output DIFFERENCE,
  output BORROW
);

  wire and_1_out, and_2_out, and_3_out, not_1_out, xor_1_out;

  not not_1 (not_1_out, A);
  xor xor_1 (xor_1_out, A, B);
  and and_1 (and_1_out, not_1_out, B);
  and and_2 (and_2_out, not_1_out, C);
  and and_3 (and_3_out, B, C);
  xor xor_2 (DIFFERENCE, xor_1_out, C);
  or or_1 (BORROW, and_1_out, and_2_out, and_3_out);
endmodule
